// Logisim project ALU.circ as structural Verilog
module my_adder (
  input  A,
  input  B,
  output SUM,
  output CARRY
);

  xor xor_1 (SUM, A, B);
  and and_1 (CARRY, A, B);
endmodule

module full_adder (
  input  A,
  input  B,
  input  CIN,
  output SUM,
  output COUT
);

  wire and_1_out, and_2_out, xor_1_out;

  xor xor_1 (xor_1_out, A, B);
  and and_1 (and_1_out, A, B);
  and and_2 (and_2_out, xor_1_out, CIN);
  xor xor_2 (SUM, xor_1_out, CIN);
  or or_1 (COUT, and_2_out, and_1_out);
endmodule

module full_4bit_adder (
  input  CIN,
  input  A1,
  input  A2,
  input  A3,
  input  A4,
  input  B1,
  input  B2,
  input  B3,
  input  B4,
  output S1,
  output S2,
  output S3,
  output S4,
  output COUT
);

  wire full_adder_1_p2, full_adder_2_p2, full_adder_3_p2;

  // full_adder full_adder_1: pin names not known; wires that end beside it: S1, full_adder_1_p2
  // full_adder full_adder_2: pin names not known; wires that end beside it: S2, full_adder_2_p2
  // full_adder full_adder_3: pin names not known; wires that end beside it: S3, full_adder_3_p2
  // full_adder full_adder_4: pin names not known; wires that end beside it: S4, COUT
endmodule

module full_8bit_adder (
  input  CIN,
  input  A1,
  input  A2,
  input  A3,
  input  A4,
  input  A5,
  input  A6,
  input  A7,
  input  A8,
  input  B1,
  input  B2,
  input  B3,
  input  B4,
  input  B5,
  input  B6,
  input  B7,
  input  B8,
  output S1,
  output S2,
  output S3,
  output S4,
  output S5,
  output S6,
  output S7,
  output S8,
  output COUT
);

  wire full_4bit_adder_1_cout;

  full_4bit_adder full_4bit_adder_1 (
    .CIN(CIN), .A1(A1), .A2(A2), .A3(A3), .A4(A4), .B1(B1), .B2(B2), .B3(B3), .B4(B4), .S1(S1), .S2(S2),
    .S3(S3), .S4(S4), .COUT(full_4bit_adder_1_cout));
  full_4bit_adder full_4bit_adder_2 (
    .CIN(full_4bit_adder_1_cout), .A1(A5), .A2(A6), .A3(A7), .A4(A8), .B1(B5), .B2(B6), .B3(B7), .B4(B8),
    .S1(S5), .S2(S6), .S3(S7), .S4(S8), .COUT(COUT));
endmodule

module and_8bit (
  input  A1,
  input  A2,
  input  A3,
  input  A4,
  input  A5,
  input  A6,
  input  A7,
  input  A8,
  input  B1,
  input  B2,
  input  B3,
  input  B4,
  input  B5,
  input  B6,
  input  B7,
  input  B8,
  output O1,
  output O2,
  output O3,
  output O4,
  output O5,
  output O6,
  output O7,
  output O8
);

  and and_1 (O1, A1, B1);
  and and_2 (O2, A2, B2);
  and and_3 (O3, A3, B3);
  and and_4 (O4, A4, B4);
  and and_5 (O5, A5, B5);
  and and_6 (O6, A6, B6);
  and and_7 (O7, A7, B7);
  and and_8 (O8, A8, B8);
endmodule

module or_8bit (
  input  A1,
  input  A2,
  input  A3,
  input  A4,
  input  A5,
  input  A6,
  input  A7,
  input  A8,
  input  B1,
  input  B2,
  input  B3,
  input  B4,
  input  B5,
  input  B6,
  input  B7,
  input  B8,
  output O1,
  output O2,
  output O3,
  output O4,
  output O5,
  output O6,
  output O7,
  output O8
);

  or or_1 (O1, A1, B1);
  or or_2 (O2, A2, B2);
  or or_3 (O3, A3, B3);
  or or_4 (O4, A4, B4);
  or or_5 (O5, A5, B5);
  or or_6 (O6, A6, B6);
  or or_7 (O7, A7, B7);
  or or_8 (O8, A8, B8);
endmodule

module xor_8bit (
  input  A1,
  input  A2,
  input  A3,
  input  A4,
  input  A5,
  input  A6,
  input  A7,
  input  A8,
  input  B1,
  input  B2,
  input  B3,
  input  B4,
  input  B5,
  input  B6,
  input  B7,
  input  B8,
  output O1,
  output O2,
  output O3,
  output O4,
  output O5,
  output O6,
  output O7,
  output O8
);

  xor xor_1 (O1, A1, B1);
  xor xor_2 (O2, A2, B2);
  xor xor_3 (O3, A3, B3);
  xor xor_4 (O4, A4, B4);
  xor xor_5 (O5, A5, B5);
  xor xor_6 (O6, A6, B6);
  xor xor_7 (O7, A7, B7);
  xor xor_8 (O8, A8, B8);
endmodule

module not_8bit (
  input  A1,
  input  A2,
  input  A3,
  input  A4,
  input  A5,
  input  A6,
  input  A7,
  input  A8,
  output O1,
  output O2,
  output O3,
  output O4,
  output O5,
  output O6,
  output O7,
  output O8
);

  not not_1 (O1, A1);
  not not_2 (O2, A2);
  not not_3 (O3, A3);
  not not_4 (O4, A4);
  not not_5 (O5, A5);
  not not_6 (O6, A6);
  not not_7 (O7, A7);
  not not_8 (O8, A8);
endmodule

module sub_8bit (
  input  A1,
  input  A2,
  input  A3,
  input  A4,
  input  A5,
  input  A6,
  input  A7,
  input  A8,
  input  B1,
  input  B2,
  input  B3,
  input  B4,
  input  B5,
  input  B6,
  input  B7,
  input  B8,
  output out_17,
  output out_18,
  output out_19,
  output out_20,
  output out_21,
  output out_22,
  output out_23,
  output out_24
);

  wire not_8bit_1_o1, not_8bit_1_o2, not_8bit_1_o3, not_8bit_1_o4, not_8bit_1_o5, not_8bit_1_o6,
       not_8bit_1_o7, not_8bit_1_o8;

  not_8bit not_8bit_1 (
    .A1(B1), .A2(B2), .A3(B3), .A4(B4), .A5(B5), .A6(B6), .A7(B7), .A8(B8), .O1(not_8bit_1_o1),
    .O2(not_8bit_1_o2), .O3(not_8bit_1_o3), .O4(not_8bit_1_o4), .O5(not_8bit_1_o5), .O6(not_8bit_1_o6),
    .O7(not_8bit_1_o7), .O8(not_8bit_1_o8));
  full_8bit_adder full_8bit_adder_1 (
    .CIN(1'b1), .A1(A1), .A2(A2), .A3(A3), .A4(A4), .A5(A5), .A6(A6), .A7(A7), .A8(A8), .B1(not_8bit_1_o1),
    .B2(not_8bit_1_o2), .B3(not_8bit_1_o3), .B4(not_8bit_1_o4), .B5(not_8bit_1_o5), .B6(not_8bit_1_o6),
    .B7(not_8bit_1_o7), .B8(not_8bit_1_o8), .S1(out_17), .S2(out_18), .S3(out_19), .S4(out_20), .S5(out_21),
    .S6(out_22), .S7(out_23), .S8(out_24));  // open: COUT
endmodule

module mult_8bit (
  input  A1,
  input  A2,
  input  A3,
  input  A4,
  input  B1,
  input  B2,
  input  B3,
  input  B4,
  output O1,
  output O2,
  output O3,
  output O4,
  output O5,
  output O6,
  output O7,
  output O8
);

  wire A1B2_out, A1B3_out, A1B4_out, A2B1_out, A2B2_out, A2B3_out, A2B4_out, A3B1_out, A3B2_out, A3B3_out,
       A3B4_out, A4B1_out, A4B2_out, A4B3_out, A4BA_out, full_adder_1_cout, full_adder_1_sum,
       full_adder_2_cout, full_adder_2_sum, full_adder_3_cout, full_adder_4_cout, full_adder_4_sum,
       full_adder_5_cout, full_adder_6_cout, full_adder_6_sum, full_adder_7_cout, full_adder_8_cout,
       my_adder_1_carry;

  and A1B1 (O1, B1, A1);
  and A2B1 (A2B1_out, B1, A2);
  and A3B1 (A3B1_out, B1, A3);
  and A4B1 (A4B1_out, B1, A4);
  and A1B2 (A1B2_out, B2, A1);
  and A2B2 (A2B2_out, B2, A2);
  and A3B2 (A3B2_out, B2, A3);
  and A4B2 (A4B2_out, B2, A4);
  and A1B3 (A1B3_out, B3, A1);
  and A2B3 (A2B3_out, B3, A2);
  and A3B3 (A3B3_out, B3, A3);
  and A4B3 (A4B3_out, B3, A4);
  and A1B4 (A1B4_out, B4, A1);
  and A2B4 (A2B4_out, B4, A2);
  and A3B4 (A3B4_out, B4, A3);
  and A4BA (A4BA_out, B4, A4);
  full_adder full_adder_1 (
    .A(full_adder_5_cout), .B(A1B4_out), .CIN(A2B3_out), .SUM(full_adder_1_sum), .COUT(full_adder_1_cout));
  full_adder full_adder_2 (
    .A(full_adder_8_cout), .B(A2B4_out), .CIN(A3B3_out), .SUM(full_adder_2_sum), .COUT(full_adder_2_cout));
  full_adder full_adder_3 (.A(full_adder_7_cout), .B(A3B4_out), .CIN(A4B3_out), .SUM(O6), .COUT(full_adder_3_cout));
  my_adder my_adder_1 (.A(A1B2_out), .B(A2B1_out), .SUM(O2), .CARRY(my_adder_1_carry));
  full_adder full_adder_4 (
    .A(my_adder_1_carry), .B(A1B3_out), .CIN(A2B2_out), .SUM(full_adder_4_sum), .COUT(full_adder_4_cout));
  my_adder my_adder_2 (.A(full_adder_3_cout), .B(A4BA_out), .SUM(O7), .CARRY(O8));
  full_adder full_adder_5 (
    .A(full_adder_4_sum), .B(full_adder_4_cout), .CIN(A3B1_out), .SUM(O3), .COUT(full_adder_5_cout));
  full_adder full_adder_6 (
    .A(full_adder_1_sum), .B(full_adder_1_cout), .CIN(A3B2_out), .SUM(full_adder_6_sum),
    .COUT(full_adder_6_cout));
  full_adder full_adder_7 (
    .A(full_adder_2_sum), .B(full_adder_2_cout), .CIN(A4B2_out), .SUM(O5), .COUT(full_adder_7_cout));
  full_adder full_adder_8 (
    .A(full_adder_6_sum), .B(full_adder_6_cout), .CIN(A4B1_out), .SUM(O4), .COUT(full_adder_8_cout));
endmodule
